// Logisim project Game.circ as structural Verilog
module main (
);

  wire clock, oneasteroidgenerator_1_out_4;
  wire [31:0] cascada_1_lfv, cascada_1_out_3, cascada_1_out_4, cascada_1_out_5, cascada_1_out_6,
       cascada_1_out_7, cascada_1_out_8, cascada_1_out_9, cascada_1_out_10, cascada_1_out_11,
       cascada_1_out_12, cascada_1_out_13, cascada_1_out_14, cascada_1_out_15, cascada_1_out_16,
       cascada_1_out_17, cascada_1_out_18, cascada_1_out_19, cascada_1_out_20, cascada_1_out_22,
       cascada_1_out_23, cascada_1_out_24, cascada_1_out_25, cascada_1_out_26, cascada_1_out_27,
       cascada_1_out_28, cascada_1_out_29, cascada_1_out_30, cascada_1_out_31, cascada_1_out_32,
       cascada_1_out_33, cascada_1_out_34, oneasteroidgenerator_1_out_3;

  Clock clock_1 (.out(clock));
  oneasteroidgenerator oneasteroidgenerator_1 (
    .out_3(oneasteroidgenerator_1_out_3), .out_4(oneasteroidgenerator_1_out_4), .lfv(cascada_1_lfv),
    .clock(clock));
  Cascada cascada_1 (
    .INPUT(oneasteroidgenerator_1_out_3), .in_2(oneasteroidgenerator_1_out_4), .lfv(cascada_1_lfv),
    .out_3(cascada_1_out_3), .out_4(cascada_1_out_4), .out_5(cascada_1_out_5), .out_6(cascada_1_out_6),
    .out_7(cascada_1_out_7), .out_8(cascada_1_out_8), .out_9(cascada_1_out_9), .out_10(cascada_1_out_10),
    .out_11(cascada_1_out_11), .out_12(cascada_1_out_12), .out_13(cascada_1_out_13),
    .out_14(cascada_1_out_14), .out_15(cascada_1_out_15), .out_16(cascada_1_out_16),
    .out_17(cascada_1_out_17), .out_18(cascada_1_out_18), .out_19(cascada_1_out_19),
    .out_20(cascada_1_out_20), .out_22(cascada_1_out_22), .out_23(cascada_1_out_23),
    .out_24(cascada_1_out_24), .out_25(cascada_1_out_25), .out_26(cascada_1_out_26),
    .out_27(cascada_1_out_27), .out_28(cascada_1_out_28), .out_29(cascada_1_out_29),
    .out_30(cascada_1_out_30), .out_31(cascada_1_out_31), .out_32(cascada_1_out_32),
    .out_33(cascada_1_out_33), .out_34(cascada_1_out_34));
  DotMatrix #(.inputtype("row"), .matrixcols(32), .matrixrows(32)) dotmatrix_1 (
    .row0(cascada_1_out_3), .row1(cascada_1_out_4), .row2(cascada_1_out_5), .row3(cascada_1_out_6),
    .row4(cascada_1_out_7), .row5(cascada_1_out_8), .row6(cascada_1_out_9), .row7(cascada_1_out_10),
    .row8(cascada_1_out_11), .row9(cascada_1_out_12), .row10(cascada_1_out_13), .row11(cascada_1_out_14),
    .row12(cascada_1_out_15), .row13(cascada_1_out_16), .row14(cascada_1_out_17), .row15(cascada_1_out_18),
    .row16(cascada_1_out_19), .row17(cascada_1_out_20), .row18(cascada_1_out_22), .row19(cascada_1_out_23),
    .row20(cascada_1_out_24), .row21(cascada_1_out_25), .row22(cascada_1_out_26), .row23(cascada_1_out_27),
    .row24(cascada_1_out_28), .row25(cascada_1_out_29), .row26(cascada_1_out_30), .row27(cascada_1_out_31),
    .row28(cascada_1_out_32), .row29(cascada_1_out_33), .row30(cascada_1_out_34));  // open: row31
endmodule

module BarHandler (
  input  reset,
  input  R,
  input  L,
  output [31:0] \output 
);

  wire clock, L_t, Left, R_t, Reset_t, reset_t_t, Right, update;
  wire [31:0] divider_1_out, multiplexer_1_out, multiplexer_2_out, multiplier_1_out, register_1_q;

  Clock clock_1 (.out(clock));
  or or_1 (R_t, R, Right);
  or or_2 (L_t, L, Left);
  or or_3 (reset_t_t, reset, Reset_t);
  or or_4 (update, R_t, L_t, reset_t_t);
  Multiplexer #(.width(32)) multiplexer_1 (
    .in0(\output ), .in1(32'h38000), .out(multiplexer_1_out), .sel(reset_t_t));  // open: en
  Register #(.width(32)) register_1 (.D(multiplexer_1_out), .en(update), .Q(register_1_q), .clk(clock));  // open: clr
  DotMatrix #(.inputtype("row"), .matrixcols(32), .matrixrows(2)) dotmatrix_1 (.row1(\output ));  // open: row0
  // Probe on register_1_q
  Button button_1 (.out(Right));
  Multiplier #(.width(32)) multiplier_1 (.a(register_1_q), .b(32'h2), .out(multiplier_1_out));  // open: cin, cout
  Divider #(.width(32)) divider_1 (.a(register_1_q), .b(32'h2), .out(divider_1_out));  // open: upper, rem
  Button button_2 (.out(Reset_t));
  Button button_3 (.out(Left));
  Multiplexer #(.width(32)) multiplexer_2 (
    .in0(multiplier_1_out), .in1(divider_1_out), .out(multiplexer_2_out), .sel(R_t));  // open: en
  ColisionHandler colisionhandler_1 (.Entrada_sin_depurar(multiplexer_2_out), .Salida_depurada(\output ));

  // Other names for the same wires on the sheet: out[31:0] = \output 
endmodule

module ColisionHandler (
  input  [31:0] Entrada_sin_depurar,
  output [31:0] Salida_depurada
);

  wire comparator_1_eq, comparator_2_eq, comparator_3_eq, comparator_4_eq, comparator_5_eq, comparator_6_eq;
  wire [1:0] multiplexer_6_out, varcolision, varcolision1, varcolision2;
  wire [31:0] sal1, sal2;

  Comparator #(.width(32)) comparator_1 (
    .a(Entrada_sin_depurar), .b(32'h80000000), .eq(comparator_1_eq));  // open: gt, lt
  Comparator #(.width(32)) comparator_2 (.a(Entrada_sin_depurar), .b(32'h1), .eq(comparator_2_eq));  // open: gt, lt
  Multiplexer #(.width(32)) multiplexer_1 (
    .in0(Entrada_sin_depurar), .in1(32'h7), .out(sal1), .sel(comparator_1_eq));  // open: en
  Multiplexer #(.width(32)) multiplexer_2 (
    .in0(Entrada_sin_depurar), .in1(32'he0000000), .out(sal2), .sel(comparator_2_eq));  // open: en
  Comparator #(.width(32)) comparator_3 (.a(Entrada_sin_depurar), .b(sal1), .eq(comparator_3_eq));  // open: gt, lt
  Comparator #(.width(32)) comparator_4 (.a(Entrada_sin_depurar), .b(sal2), .eq(comparator_4_eq));  // open: gt, lt
  Multiplexer #(.width(2)) multiplexer_3 (
    .in0(2'b00), .in1(2'b10), .out(varcolision1), .sel(comparator_3_eq));  // open: en
  Multiplexer #(.width(2)) multiplexer_4 (
    .in0(2'b01), .in1(2'b10), .out(varcolision2), .sel(comparator_4_eq));  // open: en
  Multiplexer #(.select(2), .width(32)) multiplexer_5 (
    .in0(sal1), .in1(sal2), .in3(Entrada_sin_depurar), .out(Salida_depurada), .sel(varcolision));  // open: in2, en
  Multiplexer #(.width(2)) multiplexer_6 (
    .in0(varcolision2), .in1(varcolision1), .out(multiplexer_6_out), .sel(comparator_5_eq));  // open: en
  Comparator #(.width(2)) comparator_5 (.a(varcolision1), .b(2'b00), .eq(comparator_5_eq));  // open: gt, lt
  Comparator #(.width(2)) comparator_6 (.a(varcolision1), .b(varcolision2), .eq(comparator_6_eq));  // open: gt, lt
  Multiplexer #(.width(2)) multiplexer_7 (
    .in0(multiplexer_6_out), .in1(2'b11), .out(varcolision), .sel(comparator_6_eq));  // open: en

  // Other names for the same wires on the sheet: colisioninput[31:0] = Entrada_sin_depurar
endmodule

module AsteroidController (
  output [31:0] out_1
);

  wire clock, clock_1_out, t_ff_1_q, t_ff_2_q, t_ff_2_qn;
  wire [31:0] a, b, c, d, e, f;

  Clock clock_1 (.out(clock_1_out));
  T_Flip_Flop t_ff_1 (.clk(clock_1_out), .T(clock_1_out), .Q(t_ff_1_q));  // open: Qn, preset, reset, en
  T_Flip_Flop t_ff_2 (.clk(t_ff_1_q), .T(t_ff_1_q), .Q(t_ff_2_q), .Qn(t_ff_2_qn));  // open: preset, reset, en
  T_Flip_Flop t_ff_3 (.clk(t_ff_2_qn), .T(t_ff_2_qn), .Q(clock));  // open: Qn, preset, reset, en
  Random #(.width(32)) random_1 (.clk(clock_1_out), .out(a));  // open: next, clr
  Random #(.width(32)) random_2 (.clk(clock_1_out), .out(b));  // open: next, clr
  Random #(.width(32), .trigger("falling")) random_3 (.clk(t_ff_1_q), .out(c));  // open: next, clr
  Random #(.width(32)) random_4 (.clk(t_ff_1_q), .out(d));  // open: next, clr
  Random #(.width(32)) random_5 (.clk(t_ff_2_q), .out(e));  // open: next, clr
  Random #(.width(32)) random_6 (.clk(t_ff_2_q), .out(f));  // open: next, clr
  DotMatrix #(.inputtype("row"), .matrixcols(32), .matrixrows(2)) dotmatrix_1 (.row0(out_1));  // open: row1
  assign out_1 = a & b & c & d & e & f;  // AND_Gate and_1, 32 bits wide
endmodule

module Cascada (
  input  [31:0] INPUT,
  input  in_2,
  output [31:0] out_3,
  output [31:0] out_4,
  output [31:0] out_5,
  output [31:0] out_6,
  output [31:0] out_7,
  output [31:0] out_8,
  output [31:0] out_9,
  output [31:0] out_10,
  output [31:0] out_11,
  output [31:0] out_12,
  output [31:0] out_13,
  output [31:0] out_14,
  output [31:0] out_15,
  output [31:0] out_16,
  output [31:0] out_17,
  output [31:0] out_18,
  output [31:0] out_19,
  output [31:0] out_20,
  output [31:0] lfv,
  output [31:0] out_22,
  output [31:0] out_23,
  output [31:0] out_24,
  output [31:0] out_25,
  output [31:0] out_26,
  output [31:0] out_27,
  output [31:0] out_28,
  output [31:0] out_29,
  output [31:0] out_30,
  output [31:0] out_31,
  output [31:0] out_32,
  output [31:0] out_33,
  output [31:0] out_34
);

  Register #(.width(32)) register_1 (.D(INPUT), .Q(lfv), .clk(in_2));  // open: en, clr
  Register #(.width(32)) register_2 (.D(out_8), .Q(out_9), .clk(in_2));  // open: en, clr
  Register #(.width(32)) register_3 (.D(out_14), .Q(out_15), .clk(in_2));  // open: en, clr
  Register #(.width(32)) register_4 (.D(out_20), .Q(out_22), .clk(in_2));  // open: en, clr
  Register #(.width(32)) register_5 (.D(out_27), .Q(out_28), .clk(in_2));  // open: en, clr
  Register #(.width(32)) register_6 (.D(out_33), .Q(out_34), .clk(in_2));  // open: en, clr
  Register #(.width(32)) register_7 (.D(lfv), .Q(out_4), .clk(in_2));  // open: en, clr
  Register #(.width(32)) register_8 (.D(out_9), .Q(out_10), .clk(in_2));  // open: en, clr
  Register #(.width(32)) register_9 (.D(out_15), .Q(out_16), .clk(in_2));  // open: en, clr
  Register #(.width(32)) register_10 (.D(out_22), .Q(out_23), .clk(in_2));  // open: en, clr
  Register #(.width(32)) register_11 (.D(out_28), .Q(out_29), .clk(in_2));  // open: en, clr
  Register #(.width(32)) register_12 (.D(out_4), .Q(out_5), .clk(in_2));  // open: en, clr
  Register #(.width(32)) register_13 (.D(out_10), .Q(out_11), .clk(in_2));  // open: en, clr
  Register #(.width(32)) register_14 (.D(out_16), .Q(out_17), .clk(in_2));  // open: en, clr
  Register #(.width(32)) register_15 (.D(out_23), .Q(out_24), .clk(in_2));  // open: en, clr
  Register #(.width(32)) register_16 (.D(out_29), .Q(out_30), .clk(in_2));  // open: en, clr
  Register #(.width(32)) register_17 (.D(out_5), .Q(out_6), .clk(in_2));  // open: en, clr
  Register #(.width(32)) register_18 (.D(out_11), .Q(out_12), .clk(in_2));  // open: en, clr
  Register #(.width(32)) register_19 (.D(out_17), .Q(out_18), .clk(in_2));  // open: en, clr
  Register #(.width(32)) register_20 (.D(out_24), .Q(out_25), .clk(in_2));  // open: en, clr
  Register #(.width(32)) register_21 (.D(out_30), .Q(out_31), .clk(in_2));  // open: en, clr
  Register #(.width(32)) register_22 (.D(out_6), .Q(out_7), .clk(in_2));  // open: en, clr
  Register #(.width(32)) register_23 (.D(out_12), .Q(out_13), .clk(in_2));  // open: en, clr
  Register #(.width(32)) register_24 (.D(out_18), .Q(out_19), .clk(in_2));  // open: en, clr
  Register #(.width(32)) register_25 (.D(out_25), .Q(out_26), .clk(in_2));  // open: en, clr
  Register #(.width(32)) register_26 (.D(out_31), .Q(out_32), .clk(in_2));  // open: en, clr
  Register #(.width(32)) register_27 (.D(out_7), .Q(out_8), .clk(in_2));  // open: en, clr
  Register #(.width(32)) register_28 (.D(out_13), .Q(out_14), .clk(in_2));  // open: en, clr
  Register #(.width(32)) register_29 (.D(out_19), .Q(out_20), .clk(in_2));  // open: en, clr
  Register #(.width(32)) register_30 (.D(out_26), .Q(out_27), .clk(in_2));  // open: en, clr
  Register #(.width(32)) register_31 (.D(out_32), .Q(out_33), .clk(in_2));  // open: en, clr

  assign out_3 = lfv;

  // Other names for the same wires on the sheet: clock = in_2
endmodule

// 1
module respaldo (
);

  wire and_3_out, and_4_out, CLOCK, clock_1_out, clock_t, comparator_1_eq, comparator_2_eq, comparator_3_eq,
       comparator_4_eq, comparator_5_eq, comparator_6_eq, comparator_7_eq, comparator_8_eq, comparator_9_eq,
       comparator_10_eq, comparator_12_eq, comparator_13_eq, comparator_14_eq, comparator_15_eq,
       comparator_16_eq, comparator_17_gt, comparator_18_eq, comparator_19_eq, comparator_20_eq, d_ff_1_qn,
       d_ff_2_q, keyboard_1_avail, L, LEFT, mp, nullLine, or_5_out, or_6_out, or_7_out, or_8_out, or_10_out,
       ospsignal, pp, R, RES, restart, RIGHT, spsignal, t_ff_1_q, t_ff_3_q, t_ff_4_q, update, win;
  wire [1:0] multiplexer_9_out, varcolision, varcolision1, varcolision2;
  wire [3:0] mp1, mp2, pp1, pp2;
  wire [4:0] random_1_out;
  wire [6:0] keyboard_1_data, register_33_q;
  wire [7:0] counter_3_q, counter_4_q;
  wire [31:0] _1, _2, _3, _4, _5, _6, _7, _8, _9, _10, _11, _12, _13, _14, _15, _16, _17, _18, _19, _20, _21,
       _22, _23, _24, _25, _26, _27, _28, _29, _30, _31, _32, colisiondep, colisioninput, divider_1_out,
       multiplexer_1_out, multiplexer_4_out, multiplexer_11_out, multiplier_1_out, or_1_out, register_34_q,
       sal1, sal2, sd, ssd;

  T_Flip_Flop t_ff_1 (.clk(CLOCK), .T(CLOCK), .Q(t_ff_1_q));  // open: Qn, preset, reset, en
  T_Flip_Flop t_ff_2 (.clk(t_ff_1_q), .T(t_ff_1_q), .Qn(clock_t));  // open: Q, preset, reset, en
  T_Flip_Flop t_ff_3 (.clk(clock_t), .T(clock_t), .Q(t_ff_3_q));  // open: Qn, preset, reset, en
  T_Flip_Flop t_ff_4 (.clk(t_ff_3_q), .T(t_ff_3_q), .Q(t_ff_4_q));  // open: Qn, preset, reset, en
  Random #(.width(5), .seed(50)) random_1 (.clk(t_ff_4_q), .out(random_1_out));  // open: next, clr
  Register #(.width(32)) register_1 (.D(sd), .Q(_1), .clk(clock_t));  // open: en, clr
  Register #(.width(32)) register_2 (.D(_8), .Q(_9), .clk(clock_t));  // open: en, clr
  Register #(.width(32)) register_3 (.D(_16), .Q(_17), .clk(clock_t));  // open: en, clr
  Register #(.width(32)) register_4 (.D(_24), .Q(_25), .clk(clock_t));  // open: en, clr
  Comparator #(.width(32)) comparator_1 (.a(colisioninput), .b(32'h80000000), .eq(comparator_1_eq));  // open: gt, lt
  Comparator #(.width(32)) comparator_2 (.a(colisioninput), .b(32'h1), .eq(comparator_2_eq));  // open: gt, lt
  Register #(.width(32)) register_5 (.D(_1), .Q(_2), .clk(clock_t));  // open: en, clr
  Register #(.width(32)) register_6 (.D(_9), .Q(_10), .clk(clock_t));  // open: en, clr
  Register #(.width(32)) register_7 (.D(_17), .Q(_18), .clk(clock_t));  // open: en, clr
  Register #(.width(32)) register_8 (.D(_25), .Q(_26), .clk(clock_t));  // open: en, clr
  Multiplexer #(.select(5), .width(32)) multiplexer_1 (
    .in0(32'h80000000), .in1(32'h40000000), .in2(32'h20000000), .in3(32'h10000000), .in4(32'h8000000),
    .in5(32'h4000000), .in6(32'h2000000), .in7(32'h1000000), .in8(32'h800000), .in9(32'h400000),
    .in10(32'h200000), .in11(32'h100000), .in12(32'h80000), .in13(32'h40000), .in14(32'h20000),
    .in15(32'h10000), .in16(32'h800), .in17(32'h400), .in18(32'h200), .in19(32'h100), .in20(32'h800),
    .in21(32'h400), .in22(32'h200), .in23(32'h100), .in24(32'h80), .in25(32'h40), .in26(32'h20),
    .in27(32'h10), .in28(32'h8), .in29(32'h4), .in30(32'h2), .in31(32'h1), .out(multiplexer_1_out),
    .sel(random_1_out));  // open: en
  Register #(.width(32)) register_9 (.D(_2), .Q(_3), .clk(clock_t));  // open: en, clr
  Register #(.width(32)) register_10 (.D(_10), .Q(_11), .clk(clock_t));  // open: en, clr
  Register #(.width(32)) register_11 (.D(_18), .Q(_19), .clk(clock_t));  // open: en, clr
  Register #(.width(32)) register_12 (.D(_26), .Q(_27), .clk(clock_t));  // open: en, clr
  Comparator #(.width(32)) comparator_3 (.a(colisioninput), .b(sal1), .eq(comparator_3_eq));  // open: gt, lt
  Multiplexer #(.width(32)) multiplexer_2 (
    .in0(colisioninput), .in1(32'h7), .out(sal1), .sel(comparator_1_eq));  // open: en
  Comparator #(.width(32)) comparator_4 (.a(colisioninput), .b(sal2), .eq(comparator_4_eq));  // open: gt, lt
  Multiplexer #(.width(32)) multiplexer_3 (
    .in0(colisioninput), .in1(32'he0000000), .out(sal2), .sel(comparator_2_eq));  // open: en
  Multiplexer #(.width(32)) multiplexer_4 (
    .in0({32{1'b0}}), .in1(multiplexer_1_out), .out(multiplexer_4_out), .sel(t_ff_4_q));  // open: en
  Comparator #(.width(32)) comparator_5 (.a(multiplexer_4_out), .b(_1), .eq(comparator_5_eq));  // open: gt, lt
  Register #(.width(32)) register_13 (.D(_3), .Q(_4), .clk(clock_t));  // open: en, clr
  Register #(.width(32)) register_14 (.D(_11), .Q(_12), .clk(clock_t));  // open: en, clr
  Register #(.width(32)) register_15 (.D(_19), .Q(_20), .clk(clock_t));  // open: en, clr
  Register #(.width(32)) register_16 (.D(_27), .Q(_28), .clk(clock_t));  // open: en, clr
  Multiplexer #(.width(2)) multiplexer_5 (
    .in0(2'b00), .in1(2'b10), .out(varcolision1), .sel(comparator_3_eq));  // open: en
  Multiplexer #(.width(2)) multiplexer_6 (
    .in0(2'b01), .in1(2'b10), .out(varcolision2), .sel(comparator_4_eq));  // open: en
  // Probe on sd
  Multiplexer #(.width(32)) multiplexer_7 (
    .in0(multiplexer_4_out), .in1({32{1'b0}}), .out(ssd), .sel(comparator_5_eq));  // open: en
  Comparator #(.width(32)) comparator_6 (.a(ssd), .b({32{1'b0}}), .eq(comparator_6_eq));  // open: gt, lt
  not not_1 (spsignal, comparator_6_eq);
  Register #(.width(32)) register_17 (.D(_4), .Q(_5), .clk(clock_t));  // open: en, clr
  Register #(.width(32)) register_18 (.D(_12), .Q(_13), .clk(clock_t));  // open: en, clr
  Register #(.width(32)) register_19 (.D(_20), .Q(_21), .clk(clock_t));  // open: en, clr
  Register #(.width(32)) register_20 (.D(_28), .Q(_29), .clk(clock_t));  // open: en, clr
  Register #(.width(32)) register_21 (.D(_5), .Q(_6), .clk(clock_t));  // open: en, clr
  Register #(.width(32)) register_22 (.D(_13), .Q(_14), .clk(clock_t));  // open: en, clr
  Register #(.width(32)) register_23 (.D(_21), .Q(_22), .clk(clock_t));  // open: en, clr
  Register #(.width(32)) register_24 (.D(_29), .Q(_30), .clk(clock_t));  // open: en, clr
  DotMatrix #(.inputtype("row"), .matrixcols(32), .matrixrows(32)) dotmatrix_1 (
    .row0(_1), .row1(_2), .row2(_3), .row3(_4), .row4(_5), .row5(_6), .row6(_7), .row7(_8), .row8(_9),
    .row9(_10), .row10(_11), .row11(_12), .row12(_13), .row13(_14), .row14(_15), .row15(_16), .row16(_17),
    .row17(_18), .row18(_19), .row19(_20), .row20(_21), .row21(_22), .row22(_23), .row23(_24), .row24(_25),
    .row25(_26), .row26(_27), .row27(_28), .row28(_29), .row29(_30), .row30(_31), .row31(colisiondep));
  Button RESET (.out(restart));
  Register #(.width(32)) register_25 (.D(_6), .Q(_7), .clk(clock_t));  // open: en, clr
  Register #(.width(32)) register_26 (.D(_14), .Q(_15), .clk(clock_t));  // open: en, clr
  Register #(.width(32)) register_27 (.D(_22), .Q(_23), .clk(clock_t));  // open: en, clr
  Register #(.width(32)) register_28 (.D(_30), .Q(_31), .clk(clock_t));  // open: en, clr
  Comparator #(.width(2)) comparator_7 (.a(varcolision1), .b(2'b00), .eq(comparator_7_eq));  // open: gt, lt
  Comparator #(.width(2)) comparator_8 (.a(varcolision1), .b(varcolision2), .eq(comparator_8_eq));  // open: gt, lt
  Multiplexer #(.select(2), .width(32)) multiplexer_8 (
    .in0(sal1), .in1(sal2), .in3(colisioninput), .out(colisiondep), .sel(varcolision));  // open: in2, en
  Button button_1 (.out(LEFT));
  Keyboard keyboard_1 (.clk(CLOCK), .avail(keyboard_1_avail), .data(keyboard_1_data));  // open: re, clr
  Register #(.width(32)) register_29 (.D(_7), .Q(_8), .clk(clock_t));  // open: en, clr
  Register #(.width(32)) register_30 (.D(_15), .Q(_16), .clk(clock_t));  // open: en, clr
  Register #(.width(32)) register_31 (.D(_23), .Q(_24), .clk(clock_t));  // open: en, clr
  Register #(.width(32)) register_32 (.D(_31), .Q(_32), .clk(clock_t));  // open: en, clr
  Multiplexer #(.width(2)) multiplexer_9 (
    .in0(varcolision2), .in1(varcolision1), .out(multiplexer_9_out), .sel(comparator_7_eq));  // open: en
  Multiplexer #(.width(2)) multiplexer_10 (
    .in0(multiplexer_9_out), .in1(2'b11), .out(varcolision), .sel(comparator_8_eq));  // open: en
  Button button_2 (.out(RIGHT));
  assign or_1_out = colisiondep | _32;  // OR_Gate or_1, 32 bits wide
  Comparator #(.width(7)) comparator_9 (.a(keyboard_1_data), .b(7'b1100001), .eq(comparator_9_eq));  // open: gt, lt
  Register #(.width(7)) register_33 (.D(keyboard_1_data), .Q(register_33_q), .clk(keyboard_1_avail));  // open: en, clr
  // Probe on register_33_q
  Multiplexer #(.width(32)) multiplexer_11 (
    .in0(colisiondep), .in1(32'h38000), .out(multiplexer_11_out), .sel(RES));  // open: en
  Register #(.width(32)) register_34 (
    .D(multiplexer_11_out), .en(update), .Q(register_34_q), .clk(CLOCK));  // open: clr
  Comparator #(.width(32)) comparator_10 (.a(colisiondep), .b(or_1_out), .eq(comparator_10_eq));  // open: gt, lt
  Comparator #(.width(32)) comparator_11 (.a(_32), .b({32{1'b0}}), .eq(nullLine));  // open: gt, lt
  Comparator #(.width(7)) comparator_12 (.a(keyboard_1_data), .b(7'b1100100), .eq(comparator_12_eq));  // open: gt, lt
  // Probe on register_34_q
  Hex_Digit_Display hex_digit_display_1 (.value(pp1));  // open: dp
  Hex_Digit_Display hex_digit_display_2 (.value(pp2));  // open: dp
  Hex_Digit_Display hex_digit_display_3 (.value(mp2));  // open: dp
  Hex_Digit_Display hex_digit_display_4 (.value(mp1));  // open: dp
  and and_1 (pp, comparator_10_eq, ~nullLine);  // AND_Gate
  and and_2 (mp, ~comparator_10_eq, ~nullLine);  // AND_Gate
  not not_2 (ospsignal, nullLine);
  or or_2 (R, comparator_12_eq, RIGHT);
  or or_3 (L, comparator_9_eq, LEFT);
  Multiplier #(.width(32)) multiplier_1 (.a(register_34_q), .b(32'h2), .out(multiplier_1_out));  // open: cin, cout
  Divider #(.width(32)) divider_1 (.a(register_34_q), .b(32'h2), .out(divider_1_out));  // open: upper, rem
  or or_4 (update, R, L, RES);
  Multiplexer #(.width(32)) multiplexer_12 (
    .in0(multiplier_1_out), .in1(divider_1_out), .out(colisioninput), .sel(R));  // open: en
  // Probe on _1
  // Probe on _2
  // Probe on _3
  // Probe on _4
  // Probe on _5
  // Probe on _6
  // Probe on _7
  // Probe on _8
  // Probe on _9
  // Probe on _10
  // Probe on _11
  // Probe on _12
  // Probe on _13
  // Probe on _14
  // Probe on _15
  // Probe on _16
  // Probe on _17
  // Probe on _18
  // Probe on _19
  // Probe on _20
  // Probe on _21
  // Probe on _22
  // Probe on _23
  // Probe on _24
  // Probe on _25
  // Probe on _26
  // Probe on _27
  // Probe on _28
  // Probe on _29
  // Probe on _30
  // Probe on _31
  Counter #(.width(4), .max('h9)) counter_1 (
    .Q(pp1), .clk(comparator_20_eq), .clr(or_5_out));  // open: load, D, count, carry
  or or_5 (or_5_out, win, RES);
  Counter #(.width(4), .max('h9)) counter_2 (
    .Q(mp1), .clk(comparator_19_eq), .clr(or_6_out));  // open: load, D, count, carry
  or or_6 (or_6_out, win, RES);
  Comparator #(.width(4)) comparator_13 (.a(pp1), .b(4'b0010), .eq(comparator_13_eq));  // open: gt, lt
  Comparator #(.width(4)) comparator_14 (.a(mp1), .b(4'b0010), .eq(comparator_14_eq));  // open: gt, lt
  D_Flip_Flop d_ff_1 (.clk(CLOCK), .D(CLOCK), .Qn(d_ff_1_qn));  // open: Q, preset, en, reset
  // Probe on counter_3_q
  Counter counter_3 (.count(spsignal), .Q(counter_3_q), .clk(clock_t), .clr(comparator_18_eq));  // open: load, D, carry
  Counter counter_4 (
    .count(ospsignal), .Q(counter_4_q), .clk(clock_t), .clr(comparator_18_eq));  // open: load, D, carry
  Comparator #(.width(4)) comparator_15 (.a(pp2), .b(4'b0101), .eq(comparator_15_eq));  // open: gt, lt
  and and_3 (and_3_out, comparator_13_eq, comparator_15_eq);
  Comparator #(.width(4)) comparator_16 (.a(mp2), .b(4'b0101), .eq(comparator_16_eq));  // open: gt, lt
  and and_4 (and_4_out, comparator_14_eq, comparator_16_eq);
  D_Flip_Flop d_ff_2 (.clk(CLOCK), .D(d_ff_1_qn), .Q(d_ff_2_q));  // open: Qn, preset, en, reset
  Comparator comparator_17 (.a(counter_3_q), .b(8'h2), .gt(comparator_17_gt));  // open: eq, lt
  Comparator comparator_18 (.a(counter_4_q), .b(8'h3), .eq(comparator_18_eq));  // open: gt, lt
  Counter #(.width(4), .max('ha)) counter_5 (
    .count(pp), .Q(pp2), .clk(clock_t), .clr(or_7_out));  // open: load, D, carry
  or or_7 (or_7_out, comparator_20_eq, win, RES);
  Counter #(.width(4), .max('ha)) counter_6 (
    .count(mp), .Q(mp2), .clk(clock_t), .clr(or_8_out));  // open: load, D, carry
  Comparator #(.width(4)) comparator_19 (.a(mp2), .b(4'b1010), .eq(comparator_19_eq));  // open: gt, lt
  or or_8 (or_8_out, comparator_19_eq, win, RES);
  or or_9 (RES, d_ff_2_q, restart);
  Multiplexer #(.width(32)) multiplexer_13 (.in0(ssd), .in1({32{1'b0}}), .out(sd), .sel(comparator_17_gt));  // open: en
  Clock clock_1 (.out(clock_1_out));
  Comparator #(.width(4)) comparator_20 (.a(pp2), .b(4'b1010), .eq(comparator_20_eq));  // open: gt, lt
  or or_10 (or_10_out, and_3_out, and_4_out);
  // Probe on 8'h2
  and and_5 (CLOCK, clock_1_out, ~win);  // AND_Gate
  D_Flip_Flop d_ff_3 (.clk(or_10_out), .D(or_10_out), .Q(win));  // open: Qn, preset, en, reset

  // Other names for the same wires on the sheet: out[31:0] = colisiondep; Reset = RES

  // Notes on the sheet:
  //   CONTROLS
  //   a <-  -> d
  //   PLAYER
  //   MACHINE
endmodule

module KeyBoardHandler (
);

  wire clock, keyboard_1_avail, left, right;
  wire [6:0] keyboard_1_data, register_1_q;

  Clock clock_1 (.out(clock));
  Keyboard keyboard_1 (.clk(clock), .avail(keyboard_1_avail), .data(keyboard_1_data));  // open: re, clr
  Comparator #(.width(7)) comparator_1 (.a(keyboard_1_data), .b(7'b1100001), .eq(left));  // open: gt, lt
  // Probe on register_1_q
  Register #(.width(7)) register_1 (.D(keyboard_1_data), .Q(register_1_q), .clk(keyboard_1_avail));  // open: en, clr
  Comparator #(.width(7)) comparator_2 (.a(keyboard_1_data), .b(7'b1100100), .eq(right));  // open: gt, lt
endmodule

module oneasteroidgenerator (
  input  clock,
  input  [31:0] lfv,
  output [31:0] out_3,
  output out_4
);

  wire comparator_1_eq, t_ff_1_q, t_ff_3_q, t_ff_4_q;
  wire [4:0] random_1_out;
  wire [31:0] multiplexer_1_out, multiplexer_2_out;

  T_Flip_Flop t_ff_1 (.clk(clock), .T(clock), .Q(t_ff_1_q));  // open: Qn, preset, reset, en
  T_Flip_Flop t_ff_2 (.clk(t_ff_1_q), .T(t_ff_1_q), .Qn(out_4));  // open: Q, preset, reset, en
  T_Flip_Flop t_ff_3 (.clk(out_4), .T(out_4), .Q(t_ff_3_q));  // open: Qn, preset, reset, en
  T_Flip_Flop t_ff_4 (.clk(t_ff_3_q), .T(t_ff_3_q), .Q(t_ff_4_q));  // open: Qn, preset, reset, en
  Random #(.width(5), .seed(50)) random_1 (.clk(t_ff_4_q), .out(random_1_out));  // open: next, clr
  Multiplexer #(.select(5), .width(32)) multiplexer_1 (
    .in0(32'h80000000), .in1(32'h40000000), .in2(32'h20000000), .in3(32'h10000000), .in4(32'h8000000),
    .in5(32'h4000000), .in6(32'h2000000), .in7(32'h1000000), .in8(32'h800000), .in9(32'h400000),
    .in10(32'h200000), .in11(32'h100000), .in12(32'h80000), .in13(32'h40000), .in14(32'h20000),
    .in15(32'h10000), .in16(32'h800), .in17(32'h400), .in18(32'h200), .in19(32'h100), .in20(32'h800),
    .in21(32'h400), .in22(32'h200), .in23(32'h100), .in24(32'h80), .in25(32'h40), .in26(32'h20),
    .in27(32'h10), .in28(32'h8), .in29(32'h4), .in30(32'h2), .in31(32'h1), .out(multiplexer_1_out),
    .sel(random_1_out));  // open: en
  Multiplexer #(.width(32)) multiplexer_2 (
    .in0({32{1'b0}}), .in1(multiplexer_1_out), .out(multiplexer_2_out), .sel(t_ff_4_q));  // open: en
  Comparator #(.width(32)) comparator_1 (.a(multiplexer_2_out), .b(lfv), .eq(comparator_1_eq));  // open: gt, lt
  Multiplexer #(.width(32)) multiplexer_3 (
    .in0(multiplexer_2_out), .in1({32{1'b0}}), .out(out_3), .sel(comparator_1_eq));  // open: en

  // Other names for the same wires on the sheet: _1[31:0] = lfv
endmodule

module point_counter (
  input  in_1,
  input  reset,
  input  \input ,
  output [3:0] decena,
  output [3:0] unidad,
  output win
);

  wire comparator_1_eq, comparator_2_eq, comparator_3_eq, or_1_out, or_2_out;

  Counter #(.width(4), .max('h9)) counter_1 (
    .Q(decena), .clk(comparator_3_eq), .clr(or_1_out));  // open: load, D, count, carry
  Comparator #(.width(4)) comparator_1 (.a(decena), .b(4'b0010), .eq(comparator_1_eq));  // open: gt, lt
  or or_1 (or_1_out, win, reset);
  Hex_Digit_Display hex_digit_display_1 (.value(unidad));  // open: dp
  Hex_Digit_Display hex_digit_display_2 (.value(decena));  // open: dp
  Comparator #(.width(4)) comparator_2 (.a(unidad), .b(4'b0110), .eq(comparator_2_eq));  // open: gt, lt
  and and_1 (win, comparator_1_eq, comparator_2_eq);
  Counter #(.width(4), .max('ha)) counter_2 (
    .count(in_1), .Q(unidad), .clk(\input ), .clr(or_2_out));  // open: load, D, carry
  or or_2 (or_2_out, comparator_3_eq, win, reset);
  Comparator #(.width(4)) comparator_3 (.a(unidad), .b(4'b1010), .eq(comparator_3_eq));  // open: gt, lt

  // Other names for the same wires on the sheet: RES = reset
endmodule

module PoinColision (
  input  [31:0] bar,
  input  [31:0] asteroid,
  output player,
  output machine,
  output \null 
);

  wire comparator_1_eq;
  wire [31:0] or_1_out;

  assign or_1_out = bar | asteroid;  // OR_Gate or_1, 32 bits wide
  Comparator #(.width(32)) comparator_1 (.a(bar), .b(or_1_out), .eq(comparator_1_eq));  // open: gt, lt
  and and_1 (machine, ~comparator_1_eq, ~\null );  // AND_Gate
  Comparator #(.width(32)) comparator_2 (.a(asteroid), .b({32{1'b0}}), .eq(\null ));  // open: gt, lt
  and and_2 (player, comparator_1_eq, ~\null );  // AND_Gate
endmodule
